# Fritzing sketch billow.b (saved by Fritzing 1.0.3b)
circuit board: 10cm x 3cm
breadboards: 1

parts:
  2K1 = Rotary Potentiometer (Small) [maximum_resistance=2kΩ knob_status=50% power=0.5W package=THT]
  S17 = Tactile switch 12mm [package=THT]
  2K2 = Rotary Potentiometer (Small) [maximum_resistance=2kΩ knob_status=50% power=0.5W package=THT]
  S18 = Tactile switch 12mm [package=THT]
  2K3 = Rotary Potentiometer (Small) [maximum_resistance=2kΩ knob_status=50% power=0.5W package=THT]
  2K4 = Rotary Potentiometer (Small) [maximum_resistance=2kΩ knob_status=50% power=0.5W package=THT]
  S19 = Tactile switch 12mm [package=THT]
  S20 = Tactile switch 12mm [package=THT]
  2K5 = Rotary Potentiometer (Small) [maximum_resistance=2kΩ knob_status=50% power=0.5W package=THT]
  S21 = Tactile switch 12mm [package=THT]
  J3 = female pin header, 3 pins [form="♀ (female)"]
  S22 = SPST Switch [package=switch-spdt_lock.007s]
  S23 = SPST Switch [package=switch-spdt_lock.007s]
  J4 = female pin header, 1 pin [form="♀ (female)"]
  J5 = female pin header, 1 pin [form="♀ (female)"]

nets:
  N1: 2K1.leg1, 2K2.leg1, 2K3.leg1, 2K4.leg1, 2K5.leg1, S23.P
  N2: 2K1.wiper, S17.3, S17.4
  N3: 2K1.leg2, 2K2.leg2, 2K3.leg2, 2K4.leg2, 2K5.leg2, J3.pin2
  N4: S17.1, S17.2, S18.1, S18.2, S19.1, S19.2, S20.1, S20.2, S21.1, S21.2, J3.pin3, S22.P
  N5: 2K2.wiper, S18.3, S18.4
  N6: 2K3.wiper, S19.3, S19.4
  N7: 2K4.wiper, S20.3, S20.4
  N8: 2K5.wiper, S21.3, S21.4, S22.O
  N9: J3.pin1, S23.S
  N10: S22.S, J5.pin1
  N11: S23.O, J4.pin1

notes:
  jlcjlcjlcjlc
  blueprint@poetaster.de 2024

custom parts:
  Tactile switch 12mm: 12 mm tactile switch (push button/momentary switch) from the B3F family.
